# Fritzing sketch MINIMU-9 (saved by Fritzing 0.9.2b)

parts:
  Part1 = Arduino Uno (Rev3) - ICSP
  U2 = MinIMU-9

nets:
  N1: Part1.A4/SDA, U2.SDA
  N2: Part1.A5/SCL, U2.SCL
  5V: Part1.5V, U2.VIN
  GND: Part1.GND, U2.GND

custom parts:
  MinIMU-9: MinIMU-9 9-axis compass/accelerometer/gyro. I2C interface.
